# Fritzing sketch smartpeg-pcb (saved by Fritzing 0.9.3b)
stripboards: 1

parts:
  J1 = female pin header, 8 pins [form="♀ (female)"]
  J2 = female pin header, 8 pins [form="♀ (female)"]
  D1 = Rectifier Diode [part_number=1N4007 package="300 mil [THT]"]
  J3 = female pin header, 1 pin [form="♀ (female)"]  # not connected
  J4 = female pin header, 1 pin [form="♀ (female)"]  # not connected
  J6 = female pin header, 2 pins [form="♀ (female)"]
  J5 = female pin header, 2 pins [form="♀ (female)"]
  R1 = Resistor [tolerance=±5% resistance=4.7k package=THT]
  R2 = Resistor [tolerance=±5% resistance=4.7k package=THT]
  LED1 = LED - 5mm [color="Blue (470nm)" package="5 mm [THT]"]
  R3 = Resistor [tolerance=±5% resistance=68 package=THT]
  J7 = female pin header, 4 pins [form="♀ (female)"]
  R4 = Resistor [tolerance=±5% resistance=1M package=THT]
  S1 = Toggle Switch [package=THT]
  C1 = Electrolytic Capacitor [capacitance=0.47mF voltage=16V package="100 mil [THT, electrolytic]"]
  J8 = female pin header, 4 pins [form="♀ (female)"]
  J9 = female pin header, 4 pins [form="♀ (female)"]

nets:
  N1: J1.pin2, J5.pin2, LED1.cathode, J7.pin4, R4.Pin_1, C1.-, J8.pin2
  N2: J1.pin5, R1.Pin_0, J8.pin1
  N3: J1.pin6, R2.Pin_0, J9.pin1
  N4: J2.pin1, R1.Pin_1, R2.Pin_1, J7.pin1, S1.COM, C1.+, J9.pin2
  N5: J2.pin4, J7.pin3
  N6: J2.pin5, R3.Pin_1
  N7: J2.pin7, R4.Pin_0
  N8: D1.cathode, S1.L2
  N9: D1.anode, J6.pin1
  N10: LED1.anode, R3.Pin_0
