# Fritzing sketch smartpeg (saved by Fritzing 0.9.3b)
breadboards: 1

parts:
  RHT1 = Humidity and Temperature Sensor RHT03
  WeMos_D1_Mini1 = WeMos D1 Mini  # not connected
  R1 = Resistor [tolerance=±5% resistance=47 package=THT]
  LED1 = LED - 5mm [color="Blue (470nm)" package="5 mm [THT]"]
  R2 = Resistor [tolerance=±5% resistance=1M package=THT]
  J1_-_peg_connector = female pin header, 2 pins [form="♀ (female)"]

nets:
  N1: RHT1.Vcc, J1_-_peg_connector.pin2
  N2: RHT1.GND_2, LED1.cathode, R2.Pin_0
  N3: R1.Pin_1, LED1.anode
  N4: R2.Pin_1, J1_-_peg_connector.pin1

notes:
  The WeMos Board has a slightly different pin layout as the cloned board that is used.
  It also has male-below headers that fit better on the breadboard
